# Fritzing sketch SignLanguage (saved by Fritzing 0.9.3b)
circuit board: 8.61867cm x 10.1236cm
breadboards: 1

parts:
  power_source = Square Pushbutton
  Part1 = Lilypad Arduino Board
  R1 = Basic Flex Resistor
  Part2 = Analog Digital MUX Breakout
  R2 = Resistor [tolerance=±5% resistance=220 package="2512 [SMD]"]
  Part3 = InvenSense MPU6050
  R3 = Basic Flex Resistor
  R4 = Resistor [tolerance=±5% resistance=220 package="2010 [SMD]"]
  R5 = Basic Flex Resistor
  R6 = Resistor [tolerance=±5% resistance=220 package="2010 [SMD]"]
  R7 = Basic Flex Resistor
  R8 = Resistor [tolerance=±5% resistance=220 package="2010 [SMD]"]
  R9 = Basic Flex Resistor
  R10 = Resistor [tolerance=±5% resistance=220 package="2010 [SMD]"]

nets:
  VCC: power_source.leg0, Part2.VCC, R2.Pin_1, Part3.VCC, R4.Pin_1, R6.Pin_1, R8.Pin_1, R10.Pin_1
  GND: power_source.leg1, R1.Pin_2, Part2.GND, Part3.GND, R3.Pin_2, R5.Pin_2, R7.Pin_2, R9.Pin_2
  N1: Part1.A0, Part2.SIG
  N2: Part1.A4, Part3.SDA
  N3: Part1.A5, Part3.SCL
  N4: Part1.D8, Part2.S0
  N5: Part1.D9, Part2.S1
  N6: Part1.D10, Part2.S2
  N7: Part1.MOSI/D11, Part2.S3
  N8: Part1.D7, Part2.EN
  N9: R1.pin_1, Part2.C0, R2.Pin_0
  N10: Part2.C1, R3.pin_1, R4.Pin_0
  N11: Part2.C2, R5.pin_1, R6.Pin_0
  N12: Part2.C3, R7.pin_1, R8.Pin_0
  N13: Part2.C4, R9.pin_1, R10.Pin_0
