# Fritzing sketch signLan (saved by Fritzing 0.9.3b)
circuit board: 8.8cm x 9.00427cm
breadboards: 1

parts:
  Part1 = Lilypad Arduino Board
  Switch = SWITCH_SPDT [package=kps-1290]
  S1 = Square Pushbutton
  F1 = Basic Flex Resistor
  R2 = Resistor [tolerance=±5% resistance=220 package="2512 [SMD]"]
  F2 = Basic Flex Resistor
  R4 = Resistor [tolerance=±5% resistance=220 package="2512 [SMD]"]
  F3 = Basic Flex Resistor
  R6 = Resistor [tolerance=±5% resistance=220 package="2512 [SMD]"]
  F4 = Basic Flex Resistor
  R8 = Resistor [tolerance=±5% resistance=220 package="2512 [SMD]"]
  F5 = Basic Flex Resistor
  R10 = Resistor [tolerance=±5% resistance=220 package="2512 [SMD]"]
  Part2 = Analog Digital MUX Breakout
  Part3 = InvenSense MPU6050
  Part4 = Bluetooth HC-05 Macho
  R11 = Resistor [tolerance=±5% resistance=220 package="2512 [SMD]"]
  R12 = Resistor [tolerance=±5% resistance=220 package="2512 [SMD]"]
  LED1 = LED - 5mm [color="Red (633nm)" package="5 mm [THT]"]
  LED2 = LED - 5mm [color="Red (633nm)" package="5 mm [THT]"]
  S2 = Pushbutton [package="[THT]"]
  S3 = Pushbutton [package="[THT]"]
  R13 = Resistor [tolerance=±5% resistance=220 package="2512 [SMD]"]
  R14 = Resistor [tolerance=±5% resistance=220 package="2512 [SMD]"]

nets:
  GND: Part1.GND, S1.leg1, F1.Pin_2, F2.Pin_2, F3.Pin_2, F4.Pin_2, F5.Pin_2, Part2.GND, Part3.GND, Part4.GND, R11.Pin_0, LED1.anode, LED2.anode, S2.Pin_1, S2.Pin_2, S3.Pin_3, S3.Pin_4
  VCC: Part1.VCC, Switch.S, R2.Pin_1, R4.Pin_1, R6.Pin_1, R8.Pin_1, R10.Pin_1, Part2.VCC, Part3.VCC, Part4.VCC
  N1: Part1.ISCP_MOSI, Part1.MOSI/D11, Part2.S3
  N2: Part1.A0, Part2.SIG
  N3: Part1.A4, Part3.SDA
  N4: Part1.A5, Part3.SCL
  N5: Part1.D8, Part2.S0
  N6: Part1.D9, Part2.S1
  N7: Part1.D10, Part2.S2
  N8: Part1.D6, S3.Pin_1, S3.Pin_2
  N9: Part1.D5, S2.Pin_3, S2.Pin_4
  N10: Part1.D3, Part4.TXD
  N11: Part1.D2, R12.Pin_1
  N12: Part1.TX/D1, R13.Pin_0
  N13: Part1.RX/D0, R14.Pin_0
  N14: Part1.D7, Part2.EN
  N15: Switch.P, S1.leg0
  N16: F1.pin_1, R2.Pin_0, Part2.C0
  N17: F2.pin_1, R4.Pin_0, Part2.C1
  N18: F3.pin_1, R6.Pin_0, Part2.C2
  N19: F4.pin_1, R8.Pin_0, Part2.C3
  N20: F5.pin_1, R10.Pin_0, Part2.C4
  N21: Part4.RXD, R11.Pin_1, R12.Pin_0
  N22: LED1.cathode, R13.Pin_1
  N23: LED2.cathode, R14.Pin_1
