# Fritzing sketch signLanNano (saved by Fritzing 0.9.3b)
circuit board: 7.90011cm x 8.3cm
breadboards: 1

parts:
  F1 = Basic Flex Resistor
  R2 = Resistor [tolerance=±5% resistance=220 package="2512 [SMD]"]
  F2 = Basic Flex Resistor
  R4 = Resistor [tolerance=±5% resistance=220 package="2512 [SMD]"]
  F3 = Basic Flex Resistor
  R6 = Resistor [tolerance=±5% resistance=220 package="2512 [SMD]"]
  F4 = Basic Flex Resistor
  R8 = Resistor [tolerance=±5% resistance=220 package="2512 [SMD]"]
  F5 = Basic Flex Resistor
  R10 = Resistor [tolerance=±5% resistance=220 package="2512 [SMD]"]
  Part2 = Analog Digital MUX Breakout
  Part3 = InvenSense MPU6050
  Part4 = Bluetooth HC-05 Macho
  R11 = Resistor [tolerance=±5% resistance=220 package="2512 [SMD]"]
  R12 = Resistor [tolerance=±5% resistance=220 package="2512 [SMD]"]
  LED1 = LED - 5mm [color="Red (633nm)" package="5 mm [THT]"]
  LED2 = LED - 5mm [color="Red (633nm)" package="5 mm [THT]"]
  S2 = Pushbutton [package="[THT]"]
  R13 = Resistor [tolerance=±5% resistance=220 package="2512 [SMD]"]
  R14 = Resistor [tolerance=±5% resistance=220 package="2512 [SMD]"]
  Part5 = Arduino Nano (Rev3.0)
  S4 = SPST Switch [package=switch-spdt_kit]
  S1 = Square Pushbutton
  S5 = SPST Switch [package=switch-spdt_kit]

nets:
  GND: F1.Pin_2, F2.Pin_2, F3.Pin_2, F4.Pin_2, F5.Pin_2, Part2.GND, Part3.GND, Part4.GND, R11.Pin_0, LED1.anode, LED2.anode, S2.Pin_1, S2.Pin_2, Part5.GND, S1.leg1
  N1: F1.pin_1, R2.Pin_0, Part2.C0
  VCC: R2.Pin_1, R4.Pin_1, R6.Pin_1, R8.Pin_1, R10.Pin_1, Part2.VCC, Part3.VCC, Part5.VIN, S4.S, S5.S
  N2: F2.pin_1, R4.Pin_0, Part2.C1
  N3: F3.pin_1, R6.Pin_0, Part2.C2
  N4: F4.pin_1, R8.Pin_0, Part2.C3
  N5: F5.pin_1, R10.Pin_0, Part2.C4
  N6: Part2.EN, Part5.D7
  N7: Part2.S0, Part5.D8
  N8: Part2.S1, Part5.D9
  N9: Part2.S2, Part5.D10
  N10: Part2.S3, Part5.D11/MOSI
  N11: Part2.SIG, Part5.A0
  N12: Part3.SCL, Part5.A5
  N13: Part3.SDA, Part5.A4
  N14: Part4.TXD, Part5.D2
  N15: Part4.RXD, R11.Pin_1, R12.Pin_0
  N16: Part4.VCC, S5.P
  N17: R12.Pin_1, Part5.D3
  N18: LED1.cathode, R13.Pin_1
  N19: LED2.cathode, R14.Pin_1, Part5.D0/RX
  N20: S2.Pin_3, S2.Pin_4, Part5.D5
  N21: R13.Pin_0, Part5.D1/TX
  N22: S4.P, S1.leg0
