# Fritzing sketch signLanNanomark2 (saved by Fritzing 0.9.3b)
circuit board: 7.8cm x 5.6cm
breadboards: 1

parts:
  F1 = Basic Flex Resistor
  F2 = Basic Flex Resistor
  F3 = Basic Flex Resistor
  F4 = Basic Flex Resistor
  F5 = Basic Flex Resistor
  Part3 = InvenSense MPU6050
  LED1 = LED - 5mm [color="Red (633nm)" package="5 mm [THT]"]
  LED2 = LED - 5mm [color="Red (633nm)" package="5 mm [THT]"]
  S2 = Pushbutton [package="[THT]"]
  Part5 = Arduino Nano (Rev3.0)
  S4 = SPST Switch [package=switch-spdt_kit]
  S1 = Square Pushbutton
  S5 = SPST Switch [package=switch-spdt_kit]
  R15 = Resistor [tolerance=±5% resistance=220 package=THT]
  R16 = Resistor [tolerance=±5% resistance=220 package=THT]
  R17 = Resistor [tolerance=±5% resistance=220 package=THT]
  R18 = Resistor [tolerance=±5% resistance=220 package=THT]
  R19 = Resistor [tolerance=±5% resistance=220 package=THT]
  R20 = Resistor [tolerance=±5% resistance=220 package=THT]
  R21 = Resistor [tolerance=±5% resistance=220 package=THT]
  R22 = Resistor [tolerance=±5% resistance=220 package=THT]
  R23 = Resistor [tolerance=±5% resistance=220 package=THT]
  Part4 = Bluetooth HC-05 Macho

nets:
  GND: F1.Pin_2, F2.Pin_2, F3.Pin_2, F4.Pin_2, F5.Pin_2, Part3.GND, LED1.anode, LED2.anode, S2.Pin_1, S2.Pin_2, Part5.GND, S1.leg1, R16.Pin_0, Part4.GND
  N1: F1.pin_1, Part5.A0, R23.Pin_0
  N2: F2.pin_1, Part5.A1, R22.Pin_0
  N3: F3.pin_1, Part5.A2, R21.Pin_0
  N4: F4.pin_1, Part5.A3, R20.Pin_0
  N5: F5.pin_1, Part5.A6, R19.Pin_0
  VCC: Part3.VCC, Part5.5V, S5.S, R19.Pin_1, R20.Pin_1, R21.Pin_1, R22.Pin_1, R23.Pin_1
  N6: Part3.SCL, Part5.A5
  N7: Part3.SDA, Part5.A4
  N8: LED1.cathode, R18.Pin_1
  N9: LED2.cathode, R17.Pin_1
  N10: S2.Pin_3, S2.Pin_4, Part5.D5
  N11: Part5.D1/TX, R18.Pin_0
  N12: Part5.D0/RX, R17.Pin_0
  N13: Part5.D2, Part4.TXD
  N14: Part5.D3, R15.Pin_1
  N15: Part5.VIN, S4.S
  N16: S4.P, S1.leg0
  N17: S5.P, Part4.VCC
  N18: R15.Pin_0, R16.Pin_1, Part4.RXD
